// Logisim project Koushik Banerjee_1812171642.circ as structural Verilog: 11 circuits, main circuit main
module main (
);

  NAND nand_1 ();  // open: _3, _1, _2, _4, _5, _9, _8, _10, _12, _11, _13, _6
  _3_input_OR u_3_input_or_1 ();  // open: _1, _2, _8, _3, _4, _5, _11, _12, _13, _9, _6, _10, _7, _14
  NOT not_1 ();  // open: _1, _2, _3, _4, _5, _6, _9, _8, _11, _10, _13, _12
  _3_input_AND u_3_input_and_1 ();  // open: _14, _1, _2, _13, _3, _4, _5, _9, _10, _11, _7, _12, _6, _8
  AND and_1 ();  // open: _1, _2, _4, _9, _10, _12, _13, _3, _6, _11, _5, _8
  _2_input_OR u_2_input_or_1 ();  // open: _1, _2, _4, _5, _9, _10, _12, _13, _3, _6, _8, _11
endmodule

module NAND (
  input  _1,
  input  _2,
  input  _4,
  input  _5,
  input  _9,
  input  _10,
  input  _12,
  input  _13,
  output _3,
  output _6,
  output _8,
  output _11
);

  nand nand_1 (_3, _1, _2);
  nand nand_2 (_6, _4, _5);
  nand nand_3 (_8, _9, _10);
  nand nand_4 (_11, _12, _13);
endmodule

module AND (
  input  _1,
  input  _2,
  input  _4,
  input  _5,
  input  _9,
  input  _10,
  input  _12,
  input  _13,
  output _3,
  output _6,
  output _8,
  output _11
);

  and and_1 (_3, _1, _2);
  and and_2 (_6, _4, _5);
  and and_3 (_8, _9, _10);
  and and_4 (_11, _12, _13);
endmodule

module NOT (
  input  _1,
  input  _3,
  input  _5,
  input  _9,
  input  _11,
  input  _13,
  output _2,
  output _4,
  output _6,
  output _8,
  output _10,
  output _12
);

  not not_1 (_2, _1);
  not not_2 (_4, _3);
  not not_3 (_6, _5);
  not not_4 (_8, _9);
  not not_5 (_10, _11);
  not not_6 (_12, _13);
endmodule

module _2_input_OR (
  input  _1,
  input  _2,
  input  _4,
  input  _5,
  input  _9,
  input  _10,
  input  _12,
  input  _13,
  output _3,
  output _6,
  output _8,
  output _11
);

  or or_1 (_3, _1, _2);
  or or_2 (_6, _4, _5);
  or or_3 (_8, _9, _10);
  or or_4 (_11, _12, _13);
endmodule

module _3_input_OR (
  input  _14,
  input  _1,
  input  _2,
  input  _8,
  input  _3,
  input  _4,
  input  _5,
  input  _11,
  input  _12,
  input  _13,
  input  _7,
  output _9,
  output _6,
  output _10
);

  wire or_1_out, or_2_out, or_3_out;

  or or_1 (or_1_out, _1, _2);
  or or_2 (or_2_out, _3, _4);
  or or_3 (or_3_out, _11, _12);
  or or_4 (_9, or_1_out, _8);
  or or_5 (_6, or_2_out, _5);
  or or_6 (_10, or_3_out, _13);
endmodule

module _3_input_AND (
  input  _14,
  input  _1,
  input  _2,
  input  _13,
  input  _3,
  input  _4,
  input  _5,
  input  _9,
  input  _10,
  input  _11,
  input  _7,
  output _12,
  output _6,
  output _8
);

  wire and_1_out, and_2_out, and_3_out;

  and and_1 (and_1_out, _1, _2);
  and and_2 (and_2_out, _3, _4);
  and and_3 (and_3_out, _9, _10);
  and and_4 (_12, and_1_out, _13);
  and and_5 (_6, and_2_out, _5);
  and and_6 (_8, and_3_out, _11);
endmodule

module Minterm (
  input  A,
  input  B,
  input  C,
  output F
);

  wire n3_input_and_1__6, n3_input_and_1__8, n3_input_and_1__12;

  NOT not_1 (._1(A), ._3(B), ._5(C));  // open: _2, _4, _6, _9, _8, _11, _10, _13, _12
  _3_input_AND u_3_input_and_1 (
    ._1(A), ._2(B), ._13(C), ._3(A), ._4(B), ._5(C), ._9(C), ._10(B), ._11(A), ._12(n3_input_and_1__12),
    ._6(n3_input_and_1__6), ._8(n3_input_and_1__8));  // open: _14, _7
  _3_input_OR u_3_input_or_1 (
    ._1(n3_input_and_1__6), ._2(n3_input_and_1__12), ._8(n3_input_and_1__8), ._9(F));  // open: _3, _4, _5, _11, _12, _13, _6, _10, _7, _14
endmodule

module MAX (
  input  A,
  input  B,
  input  C,
  output F
);

  wire n3_input_and_1__12, n3_input_or_1__6, n3_input_or_1__9, n3_input_or_2__9, not_1__2, not_1__4,
       not_1__6, undriven;

  NOT not_1 (._1(A), ._2(not_1__2), ._3(B), ._4(not_1__4), ._5(C), ._6(not_1__6));  // open: _9, _8, _11, _10, _13, _12
  _3_input_OR u_3_input_or_1 (
    ._1(A), ._2(not_1__2), ._8(not_1__4), ._3(A), ._5(C), ._11(not_1__6), ._12(B), ._13(C),
    ._9(n3_input_or_1__9), ._6(n3_input_or_1__6));  // open: _4, _10, _7, _14
  _3_input_AND u_3_input_and_1 (
    ._1(n3_input_or_1__6), ._2(n3_input_or_1__9), ._13(n3_input_or_2__9), ._9(undriven), ._10(F),
    ._11(undriven), ._12(n3_input_and_1__12));  // open: _14, _3, _4, _5, _7, _6, _8
  _3_input_OR u_3_input_or_2 (
    ._1(not_1__6), ._2(B), ._8(not_1__4), ._3(not_1__6), ._4(not_1__2), ._5(not_1__4), ._9(n3_input_or_2__9),
    ._6(n3_input_and_1__12));  // open: _11, _12, _13, _10, _7, _14
endmodule

module Max (
  input  in_1,
  input  in_2,
  input  in_3
);
endmodule

module MAX_circuit (
  input  A,
  input  B,
  input  C,
  output F
);

  wire not_1_out, not_2_out, not_3_out, or_1_out, or_2_out, or_3_out, or_4_out, or_5_out;

  not not_1 (not_1_out, A);
  not not_2 (not_2_out, B);
  not not_3 (not_3_out, C);
  or or_1 (or_1_out, A, B, C);
  or or_2 (or_2_out, A, not_2_out, not_3_out);
  or or_3 (or_3_out, not_1_out, B, C);
  or or_4 (or_4_out, not_1_out, B, not_3_out);
  or or_5 (or_5_out, not_1_out, not_2_out, not_3_out);
  and and_1 (F, or_1_out, or_2_out, or_3_out, or_4_out, or_5_out);

  // Notes on the sheet:
  //   (A+B+C)(A+B'+C')(A'+B+C)(A'+B+C')(A'+B'+C')
endmodule
