// Logisim project Koushik Banerjee_1812171642.circ as structural Verilog: 16 circuits, main circuit main
module main (
);

  NAND nand_1 ();  // open: _3, _1, _2, _4, _5, _9, _8, _10, _12, _11, _13, _6
  _3_input_OR u_3_input_or_1 ();  // open: _1, _2, _8, _3, _4, _5, _11, _12, _13, _9, _6, _10, _7, _14
  NOT not_1 ();  // open: _1, _2, _3, _4, _5, _6, _9, _8, _11, _10, _13, _12
  _3_input_AND u_3_input_and_1 ();  // open: _14, _1, _2, _13, _3, _4, _5, _9, _10, _11, _7, _12, _6, _8
  AND and_1 ();  // open: _1, _2, _4, _9, _10, _12, _13, _3, _6, _11, _5, _8
  _2_input_OR u_2_input_or_1 ();  // open: _1, _2, _4, _5, _9, _10, _12, _13, _3, _6, _8, _11
endmodule

module NAND (
  input  _1,
  input  _2,
  input  _4,
  input  _5,
  input  _9,
  input  _10,
  input  _12,
  input  _13,
  output _3,
  output _6,
  output _8,
  output _11
);

  nand nand_1 (_3, _1, _2);
  nand nand_2 (_6, _4, _5);
  nand nand_3 (_8, _9, _10);
  nand nand_4 (_11, _12, _13);
endmodule

module AND (
  input  _1,
  input  _2,
  input  _4,
  input  _5,
  input  _9,
  input  _10,
  input  _12,
  input  _13,
  output _3,
  output _6,
  output _8,
  output _11
);

  and and_1 (_3, _1, _2);
  and and_2 (_6, _4, _5);
  and and_3 (_8, _9, _10);
  and and_4 (_11, _12, _13);
endmodule

module NOT (
  input  _1,
  input  _3,
  input  _5,
  input  _9,
  input  _11,
  input  _13,
  output _2,
  output _4,
  output _6,
  output _8,
  output _10,
  output _12
);

  not not_1 (_2, _1);
  not not_2 (_4, _3);
  not not_3 (_6, _5);
  not not_4 (_8, _9);
  not not_5 (_10, _11);
  not not_6 (_12, _13);
endmodule

module _2_input_OR (
  input  _1,
  input  _2,
  input  _4,
  input  _5,
  input  _9,
  input  _10,
  input  _12,
  input  _13,
  output _3,
  output _6,
  output _8,
  output _11
);

  or or_1 (_3, _1, _2);
  or or_2 (_6, _4, _5);
  or or_3 (_8, _9, _10);
  or or_4 (_11, _12, _13);
endmodule

module _3_input_OR (
  input  _14,
  input  _1,
  input  _2,
  input  _8,
  input  _3,
  input  _4,
  input  _5,
  input  _11,
  input  _12,
  input  _13,
  input  _7,
  output _9,
  output _6,
  output _10
);

  wire or_1_out, or_2_out, or_3_out;

  or or_1 (or_1_out, _1, _2);
  or or_2 (or_2_out, _3, _4);
  or or_3 (or_3_out, _11, _12);
  or or_4 (_9, or_1_out, _8);
  or or_5 (_6, or_2_out, _5);
  or or_6 (_10, or_3_out, _13);
endmodule

module _3_input_AND (
  input  _14,
  input  _1,
  input  _2,
  input  _13,
  input  _3,
  input  _4,
  input  _5,
  input  _9,
  input  _10,
  input  _11,
  input  _7,
  output _12,
  output _6,
  output _8
);

  wire and_1_out, and_2_out, and_3_out;

  and and_1 (and_1_out, _1, _2);
  and and_2 (and_2_out, _3, _4);
  and and_3 (and_3_out, _9, _10);
  and and_4 (_12, and_1_out, _13);
  and and_5 (_6, and_2_out, _5);
  and and_6 (_8, and_3_out, _11);
endmodule

module _7483_IC (
  input  C_in,
  input  B4,
  input  B3,
  input  B2,
  input  B1,
  input  A4,
  input  A3,
  input  A2,
  input  A1,
  output C_out,
  output S4,
  output S3,
  output S2,
  output S1
);

  wire and_1_out, and_2_out, and_3_out, and_4_out, and_5_out, and_6_out, and_7_out, and_8_out, or_1_out,
       or_2_out, or_3_out, xor_1_out, xor_2_out, xor_3_out, xor_4_out;

  xor xor_1 (xor_1_out, A1, B1);
  and and_1 (and_1_out, A1, B1);
  xor xor_2 (xor_2_out, A2, B2);
  and and_2 (and_2_out, A2, B2);
  xor xor_3 (xor_3_out, A3, B3);
  and and_3 (and_3_out, A3, B3);
  xor xor_4 (xor_4_out, A4, B4);
  and and_4 (and_4_out, A4, B4);
  and and_5 (and_5_out, xor_1_out, C_in);
  xor xor_5 (S1, xor_1_out, C_in);
  xor xor_6 (S2, xor_2_out, or_1_out);
  and and_6 (and_6_out, xor_2_out, or_1_out);
  xor xor_7 (S3, xor_3_out, or_3_out);
  and and_7 (and_7_out, xor_3_out, or_3_out);
  xor xor_8 (S4, xor_4_out, or_2_out);
  and and_8 (and_8_out, xor_4_out, or_2_out);
  or or_1 (or_1_out, and_5_out, and_1_out);
  or or_2 (or_2_out, and_7_out, and_3_out);
  or or_3 (or_3_out, and_6_out, and_2_out);
  or or_4 (C_out, and_8_out, and_4_out);
endmodule

module XOR_IC (
  input  _1,
  input  _2,
  input  _4,
  input  _5,
  input  _10,
  input  _9,
  input  _13,
  input  _12,
  output _3,
  output _6,
  output _8,
  output _11
);

  xor xor_1 (_3, _1, _2);
  xor xor_2 (_6, _4, _5);
  xor xor_3 (_8, _10, _9);
  xor xor_4 (_11, _13, _12);
endmodule

module _4_1_IC (
  input  I0,
  input  I1,
  input  I2,
  input  I3,
  input  S1,
  input  S0,
  output out_7
);

  wire and_1_out, and_2_out, and_3_out, and_4_out, not_1_out, not_2_out, or_1_out, or_2_out;

  not not_1 (not_1_out, S0);
  not not_2 (not_2_out, S1);
  and and_1 (and_1_out, I0, not_2_out, not_1_out);
  and and_2 (and_2_out, I1, not_2_out, S0);
  and and_3 (and_3_out, I2, S1, not_1_out);
  and and_4 (and_4_out, I3, S1, S0);
  or or_1 (or_1_out, and_1_out, and_2_out);
  or or_2 (or_2_out, and_3_out, and_4_out);
  or or_3 (out_7, or_1_out, or_2_out);
endmodule

module _8_1_IC (
  input  _17,
  input  _16,
  input  _15,
  input  _14,
  input  S0,
  input  _13,
  input  _12,
  input  _11,
  input  _10,
  input  S1,
  input  S2,
  output out_12
);

  wire n4_1_ic_1_out_7, n4_1_ic_2_out_7;

  _4_1_IC u_4_1_ic_1 (.I0(_14), .I1(_15), .I2(_16), .I3(_17), .S1(S2), .S0(S1), .out_7(n4_1_ic_1_out_7));
  _4_1_IC u_4_1_ic_2 (.I0(_10), .I1(_11), .I2(_12), .I3(_13), .S1(S1), .S0(S2), .out_7(n4_1_ic_2_out_7));
  Multiplexer #(.enable("false")) multiplexer_1 (.in0(n4_1_ic_1_out_7), .in1(n4_1_ic_2_out_7), .out(out_12), .sel(S0));
endmodule

module EXP3 (
  input  D,
  input  in_2,
  input  in_3,
  input  in_4,
  output out_5
);

  _8_1_IC u_8_1_ic_1 (
    ._17(1'b1), ._16(1'b0), ._15(1'b0), ._14(1'b1), .S0(in_2), ._13(1'b0), ._12(D), ._11(D), ._10(1'b1),
    .S1(in_3), .S2(in_4), .out_12(out_5));
endmodule

module _8_1_MUX (
  input  in_1,
  input  in_2,
  input  in_3,
  input  in_4,
  input  in_5,
  input  in_6,
  output out_7
);

  _8_1_IC u_8_1_ic_1 (
    ._17(in_1), ._16(in_3), ._15(in_3), ._14(in_1), .S0(in_4), ._13(in_3), ._12(in_2), ._11(in_2),
    ._10(in_1), .S1(in_5), .S2(in_6), .out_12(out_7));
endmodule

module _4_1_function_exp1 (
  input  C,
  input  A,
  input  B,
  output out_4
);

  _4_1_IC u_4_1_ic_1 (.I0(C), .I1(C), .I2(1'b0), .I3(1'b1), .S1(A), .S0(B), .out_7(out_4));
endmodule

module _8_3_function__exp2 (
  input  in_1,
  input  in_2,
  input  in_3,
  input  in_4,
  output out_5
);

  _8_1_IC u_8_1_ic_1 (
    ._17(1'b1), ._16(1'b0), ._15(1'b0), ._14(1'b1), .S0(in_2), ._13(1'b0), ._12(in_1), ._11(in_1),
    ._10(1'b1), .S1(in_3), .S2(in_4), .out_12(out_5));
endmodule

module \design  (
  input  in_1,
  input  in_2,
  input  in_3,
  input  in_4,
  input  in_5,
  input  C,
  input  in_7,
  input  [2:0] in_8,
  input  in_9,
  input  in_10,
  input  [1:0] in_11,
  output Y
);

  _4_1_IC u_4_1_ic_1 (.I0(C), .I1(C), .I2(1'b0), .I3(1'b1), .S1(in_11[0]), .S0(in_11[1]), .out_7(Y));
  Demultiplexer #(.select(3), .enable("false")) demultiplexer_1 (
    .out0(in_1), .out1(in_2), .out2(in_3), .out3(in_4), .out4(in_5), .out5(in_7), .out6(in_9), .out7(in_10),
    .sel(in_8));  // open: in
endmodule
